# Fritzing sketch AMMA (saved by Fritzing 0.8.0b)
breadboards: 2

parts:
  R1 = Photocell (LDR) [package=THT]
  Part1 = Bluetooth Mate Silver
  Figaro_TGS_2602_Gas_Sensor1 = Figaro TGS 2602 Gas Sensor
  BMP1 = BMP085 Breakout
  Figaro_TGS_2602_Gas_Sensor2 = Figaro TGS 2602 Gas Sensor
  DHT1 = DHT11 Humitidy and Temperature Sensor
  LED1 = Blue LED - 5mm [package="5 mm [THT]"]
  M1 = DC Motor
  M2 = DC Motor
  VCC1 = 4 x AAA Battery Mount
  Part4 = SRF05 Ultrasonic Rangefinder
  R2 = Resistor [tolerance=±5% resistance=220 package=THT]
  R3 = 10k Ω Resistor [package=THT]
  Part8 = Arduino Mega 2560 (Rev3)
  Part9 = Arduino Motor Shield
  ANT1 = Antenna  # not connected
  Part10 = Arduino Motor Shield
  Part11 = Breakout Board for Electret Microphone

nets:
  N1: R1.pin_0, R2.Pin_1, Part10.A3
  VCC: R1.pin_1, Part1.VCC, Figaro_TGS_2602_Gas_Sensor1.pin_4, BMP1.VIN, Figaro_TGS_2602_Gas_Sensor2.pin_4, LED1.cathode, Part9.3.3V
  N2: Part1.RX_5V, Part8.D18/TX1
  N3: Part1.TX_5V, Part8.D19/RX1
  GND: Part1.GND, Figaro_TGS_2602_Gas_Sensor1.pin_1, BMP1.GND, Figaro_TGS_2602_Gas_Sensor2.pin_1, DHT1.GND, VCC1.-, Part4.GND, R2.Pin_0, R3.Pin_0, Part9.GND, Part10.GND, Part11.GND
  N4: Figaro_TGS_2602_Gas_Sensor1.pin_2, Part10.A0
  N5: BMP1.SCL, Part8.D21/SCL
  N6: BMP1.SDA, Part8.D20/SDA
  N7: Figaro_TGS_2602_Gas_Sensor2.pin_2, Part10.A1
  VCC_2: DHT1.VDD, Part4.VCC, Part9.5V, Part11.VCC
  N8: DHT1.DATA, Part10.A2
  N9: LED1.anode, R3.Pin_1, Part10.A5
  N10: M1.pin_1, Part9.OUT4, Part10.OUT4
  N11: M1.pin_2, Part9.OUT3, Part10.OUT3
  N12: M2.pin_1, Part9.OUT1, Part10.OUT1
  N13: M2.pin_2, Part9.OUT2, Part10.OUT2
  VIN: VCC1.+, Part9.VIN, Part10.VIN
  N14: Part10.A4, Part11.AUD

notes:
  Цифровой барометр на чипе BMP085
  Датчик звука (шума)
  Фоторезистор
  Датчик газа
  Датчик дыма
  Датчик DHT11 температуры и влажности
  3.3v
  5v
  Питание
  Сонар
  wi-fi
  Плата-драйвер для моторов
  Два DC мотора
  Датчик пламени

custom parts:
  Figaro TGS 2602 Gas Sensor: The sensing element is comprised of a metal oxide semiconductor layer formed on the alumina substrate of a sensing chip together with an integrated heater. In the presence of detectable gas, sensor conductivity increases depending on gas concentration in the air. A simple electrical circuit can convert the change in conductivity to an output signal which corresponds to the gas concentration.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
  BMP085 Breakout: A breakout for the BMP085 barometric pressure and temperature sensor
  DHT11 Humitidy and Temperature Sensor: DHT11 Humidity and Temperature Sensor
